// Logisim project 8_bit_load_only_reg.circ as structural Verilog: 1 circuit, main circuit main
module main (
  input  [7:0] _8_bit_Input,
  input  CLK__do_not_use,
  input  Enable,
  input  Reset,
  output [7:0] _8_bit_Output
);

  wire and_1_out, CLK_out, or_1_out;

  Clock CLK (.out(CLK_out));
  or or_1 (or_1_out, CLK__do_not_use, CLK_out);
  and and_1 (and_1_out, Enable, Reset);
  Hex_Digit_Display hex_digit_display_1 (.value(_8_bit_Input[7:4]));  // open: dp
  Hex_Digit_Display hex_digit_display_2 (.value(_8_bit_Input[3:0]));  // open: dp
  D_Flip_Flop d_ff_1 (
    .clk(or_1_out), .D(_8_bit_Input[7]), .Q(_8_bit_Output[7]), .en(Enable), .reset(and_1_out));  // open: Qn, preset
  D_Flip_Flop d_ff_2 (
    .clk(or_1_out), .D(_8_bit_Input[6]), .Q(_8_bit_Output[6]), .en(Enable), .reset(and_1_out));  // open: Qn, preset
  D_Flip_Flop d_ff_3 (
    .clk(or_1_out), .D(_8_bit_Input[5]), .Q(_8_bit_Output[5]), .en(Enable), .reset(and_1_out));  // open: Qn, preset
  D_Flip_Flop d_ff_4 (
    .clk(or_1_out), .D(_8_bit_Input[4]), .Q(_8_bit_Output[4]), .en(Enable), .reset(and_1_out));  // open: Qn, preset
  D_Flip_Flop d_ff_5 (
    .clk(or_1_out), .D(_8_bit_Input[3]), .Q(_8_bit_Output[3]), .en(Enable), .reset(and_1_out));  // open: Qn, preset
  D_Flip_Flop d_ff_6 (
    .clk(or_1_out), .D(_8_bit_Input[2]), .Q(_8_bit_Output[2]), .en(Enable), .reset(and_1_out));  // open: Qn, preset
  D_Flip_Flop d_ff_7 (
    .clk(or_1_out), .D(_8_bit_Input[1]), .Q(_8_bit_Output[1]), .en(Enable), .reset(and_1_out));  // open: Qn, preset
  D_Flip_Flop d_ff_8 (
    .clk(or_1_out), .D(_8_bit_Input[0]), .Q(_8_bit_Output[0]), .en(Enable), .reset(and_1_out));  // open: Qn, preset
  Hex_Digit_Display hex_digit_display_3 (.value(_8_bit_Output[3:0]));  // open: dp
  Hex_Digit_Display hex_digit_display_4 (.value(_8_bit_Output[7:4]));  // open: dp

  // Notes on the sheet:
  //   Hex Output
endmodule
