// Logisim project corg2part2.circ as structural Verilog: 1 circuit, main circuit main
module main (
  input  [3:0] RegSel,
  input  [1:0] OutBSel,
  input  MuxCSel,
  input  [3:0] FunSel,
  input  [1:0] FunSel_2,
  input  [1:0] OutASel,
  input  Enable,
  input  Reset,
  input  [1:0] MuxASel,
  input  [2:0] RegSel_2,
  input  [1:0] FunSel_3,
  input  [1:0] OutCSel,
  input  [1:0] MuxBSel,
  input  in_14,
  input  in_15,
  input  [1:0] OutCSel_2,
  input  in_17,
  input  in_18,
  input  L_H_prime,
  input  Enable_2,
  input  [1:0] FunSel_4,
  output [3:0] Z_C_N_O
);

  wire clock_1_out, not_1_out;
  wire [3:0] main_1_outa, main_1_outa_2, main_1_outb, main_1_outb_2, main_2_output, main_2_output_2,
       main_3_out_d, main_3_out_d_2, main_4_outflag;
  wire [7:0] main_2_output_3, main_3_out_c, main_4_outalu, multiplexer_1_out, multiplexer_2_out,
       multiplexer_3_out, ram_1_data;

  Hex_Digit_Display hex_digit_display_1 (.value(main_1_outa_2));  // open: dp
  Hex_Digit_Display hex_digit_display_2 (.value(multiplexer_1_out[7:4]));  // open: dp
  Hex_Digit_Display hex_digit_display_3 (.value(main_1_outb_2));  // open: dp
  Hex_Digit_Display hex_digit_display_4 (.value(main_1_outa));  // open: dp
  Hex_Digit_Display hex_digit_display_5 (.value(multiplexer_1_out[3:0]));  // open: dp
  Hex_Digit_Display hex_digit_display_6 (.value(main_2_output_2));  // open: dp
  Hex_Digit_Display hex_digit_display_7 (.value(main_1_outb));  // open: dp
  Multiplexer #(.select(2), .width(8), .enable("false")) multiplexer_1 (
    .in0({main_2_output_2, main_2_output}), .in1(ram_1_data), .in2(main_3_out_c), .in3(main_4_outalu),
    .out(multiplexer_1_out), .sel(MuxASel));
  Hex_Digit_Display hex_digit_display_8 (.value(main_2_output));  // open: dp
  part2a_main main_1 (
    ._8_bit_IN(multiplexer_1_out), .RegSel(RegSel), .Clock(clock_1_out), .FunSel(FunSel_2),
    .OutSelA(OutASel), .OutSelB(OutBSel), .OutA({main_1_outa_2, main_1_outa}),
    .OutB({main_1_outb_2, main_1_outb}));
  not not_1 (not_1_out, L_H_prime);
  Multiplexer #(.width(8), .enable("false")) multiplexer_2 (
    .in0(multiplexer_1_out), .in1({main_1_outa_2, main_1_outa}), .out(multiplexer_2_out), .sel(MuxCSel));
  Part2c_main main_2 (
    .FunSel(FunSel_4), .\Input_Pın___8_bit (ram_1_data), .L_prime_H(not_1_out), .ENABLE(Enable_2),
    .Output({main_2_output_3, main_2_output_2, main_2_output}), .Clock(clock_1_out));  // open: out_7
  Hex_Digit_Display hex_digit_display_9 (.value(main_3_out_d_2));  // open: dp
  Multiplexer #(.select(2), .width(8), .enable("false")) multiplexer_3 (
    .in0(multiplexer_3_out), .in1({main_2_output_2, main_2_output}), .in2(ram_1_data), .in3(main_4_outalu),
    .out(multiplexer_3_out), .sel(MuxBSel));
  Hex_Digit_Display hex_digit_display_10 (.value(main_3_out_d));  // open: dp
  part2b_main main_3 (
    ._8_bit_IN(multiplexer_3_out), .RegSel(RegSel_2), .Clock(clock_1_out), .FunSel(FunSel_3),
    .OutSelC(OutCSel_2), .OutSelD(OutCSel), .OUT_C(main_3_out_c), .OUT_D({main_3_out_d_2, main_3_out_d}));
  Hex_Digit_Display hex_digit_display_11 (.value(main_3_out_c[3:0]));  // open: dp
  Hex_Digit_Display hex_digit_display_12 (.value(main_3_out_c[7:4]));  // open: dp
  Hex_Digit_Display hex_digit_display_13 (.value(main_4_outalu[7:4]));  // open: dp
  corg_P2_main main_4 (
    .A(multiplexer_2_out), .B({main_1_outb_2, main_1_outb}), .FunSel(FunSel), .OutALU(main_4_outalu),
    .Cin(Z_C_N_O[2]), .OutFlag(main_4_outflag));
  Hex_Digit_Display hex_digit_display_14 (.value(main_4_outalu[3:0]));  // open: dp
  _4_bit_load_only_reg_main main_5 (
    .Cin(Z_C_N_O), .Enable(Enable), .CLK_for_library(clock_1_out), .OutFlag(main_4_outflag), .Reset(Reset));
  Hex_Digit_Display hex_digit_display_15 (.value(ram_1_data[7:4]));  // open: dp
  Hex_Digit_Display hex_digit_display_16 (.value(ram_1_data[3:0]));  // open: dp
  Clock clock_1 (.out(clock_1_out));
  RAM #(.bus("separate")) ram_1 (
    .addr({main_3_out_d_2, main_3_out_d}), .din(main_4_outalu), .data(ram_1_data), .str(in_14), .sel(in_17),
    .clk(clock_1_out), .ld(in_18), .clr(in_15));

  // Notes on the sheet:
  //   OutA
  //   MuxAOut
  //   IROut (0-7)
  //   OutB
  //   Adress Reg OutD
  //   Adress Reg OutC
  //   OutALU
  //   Memory Output
endmodule
