// Logisim project Project3.circ as structural Verilog: 1 circuit, main circuit main
module main (
  input  Z_C_N_O_Reset,
  input  Clear,
  output [3:0] ALU_Z_C_N_O
);

  wire CLOCK, IR_Enable, IR_L_H_prime, MUXC, not_1_out, Ram_LOAD, Ram_Write;
  wire [1:0] IR_FUNSEL, MUXA, MUXB, OutAsel, OutBsel, OutCsel, OutDsel, PC_AR_SP_funsel, R0_R3_funsel;
  wire [2:0] PC_AR_SP_regsel;
  wire [3:0] ALU_funsel, main_1_outa, main_1_outa_2, main_1_outb, main_1_outb_2, main_3_out_d,
       main_3_out_d_2, main_4_outflag, R0_R3_regsel;
  wire [7:0] main_3_out_c, main_4_outalu, multiplexer_1_out, multiplexer_2_out, multiplexer_3_out, ram_1_data;
  wire [15:0] INSTRUCTIONS;

  Hex_Digit_Display hex_digit_display_1 (.value(main_1_outa_2));  // open: dp
  Hex_Digit_Display hex_digit_display_2 (.value(multiplexer_1_out[7:4]));  // open: dp
  Hex_Digit_Display hex_digit_display_3 (.value(INSTRUCTIONS[7:4]));  // open: dp
  Hex_Digit_Display hex_digit_display_4 (.value(main_1_outa));  // open: dp
  Hex_Digit_Display hex_digit_display_5 (.value(main_1_outb_2));  // open: dp
  Hex_Digit_Display hex_digit_display_6 (.value(multiplexer_1_out[3:0]));  // open: dp
  Hex_Digit_Display hex_digit_display_7 (.value(INSTRUCTIONS[3:0]));  // open: dp
  Hex_Digit_Display hex_digit_display_8 (.value(main_1_outb));  // open: dp
  Multiplexer #(.select(2), .width(8), .enable("false")) multiplexer_1 (
    .in0(INSTRUCTIONS[7:0]), .in1(ram_1_data), .in2(main_3_out_c), .in3(main_4_outalu),
    .out(multiplexer_1_out), .sel(MUXA));
  part2a_main main_1 (
    ._8_bit_IN(multiplexer_1_out), .RegSel(R0_R3_regsel), .Clock(CLOCK), .FunSel(R0_R3_funsel),
    .OutSelA(OutAsel), .OutSelB(OutBsel), .OutA({main_1_outa_2, main_1_outa}),
    .OutB({main_1_outb_2, main_1_outb}));
  not not_1 (not_1_out, IR_L_H_prime);
  Multiplexer #(.width(8), .enable("false")) multiplexer_2 (
    .in0(multiplexer_1_out), .in1({main_1_outa_2, main_1_outa}), .out(multiplexer_2_out), .sel(MUXC));
  Part2c_main main_2 (
    .FunSel(IR_FUNSEL), .\Input_Pın___8_bit (ram_1_data), .L_prime_H(not_1_out), .ENABLE(IR_Enable),
    .Output(INSTRUCTIONS), .Clock(CLOCK));  // open: out_7
  Hex_Digit_Display hex_digit_display_9 (.value(main_3_out_d_2));  // open: dp
  Multiplexer #(.select(2), .width(8), .enable("false")) multiplexer_3 (
    .in0(multiplexer_3_out), .in1(INSTRUCTIONS[7:0]), .in2(ram_1_data), .in3(main_4_outalu),
    .out(multiplexer_3_out), .sel(MUXB));
  Hex_Digit_Display hex_digit_display_10 (.value(main_3_out_d));  // open: dp
  part2b_main main_3 (
    ._8_bit_IN(multiplexer_3_out), .RegSel(PC_AR_SP_regsel), .Clock(CLOCK), .FunSel(PC_AR_SP_funsel),
    .OutSelC(OutCsel), .OutSelD(OutDsel), .OUT_C(main_3_out_c), .OUT_D({main_3_out_d_2, main_3_out_d}));
  Hex_Digit_Display hex_digit_display_11 (.value(main_3_out_c[7:4]));  // open: dp
  Hex_Digit_Display hex_digit_display_12 (.value(main_3_out_c[3:0]));  // open: dp
  Hex_Digit_Display hex_digit_display_13 (.value(main_4_outalu[7:4]));  // open: dp
  corg_P2_main main_4 (
    .A(multiplexer_2_out), .B({main_1_outb_2, main_1_outb}), .FunSel(ALU_funsel), .OutALU(main_4_outalu),
    .Cin(ALU_Z_C_N_O[2]), .OutFlag(main_4_outflag));
  Hex_Digit_Display hex_digit_display_14 (.value(main_4_outalu[3:0]));  // open: dp
  _4_bit_load_only_reg_main main_5 (
    .Cin(ALU_Z_C_N_O), .Enable(1'b1), .CLK_for_library(CLOCK), .OutFlag(main_4_outflag), .Reset(Z_C_N_O_Reset));
  Hex_Digit_Display hex_digit_display_15 (.value(ram_1_data[3:0]));  // open: dp
  Hex_Digit_Display hex_digit_display_16 (.value(ram_1_data[7:4]));  // open: dp
  RAM #(.bus("separate")) ram_1 (
    .addr({main_3_out_d_2, main_3_out_d}), .din(main_4_outalu), .data(ram_1_data), .str(Ram_Write),
    .clk(CLOCK), .ld(Ram_LOAD), .clr(Clear));  // open: sel
  Clock clock_1 (.out(CLOCK));
  Control__Unit_main main_6 (
    .Instructions(INSTRUCTIONS), .Clock(CLOCK), .Z_Flag(ALU_Z_C_N_O[3]), .MUXA(MUXA), .MUXB(MUXB),
    .MUXC(MUXC), .R0_R3_regsel(R0_R3_regsel), .PC_AR_SP_regsel(PC_AR_SP_regsel), .R0_R3_funsel(R0_R3_funsel),
    .PC_AR_SP_funsel(PC_AR_SP_funsel), .OutAsel(OutAsel), .OutBsel(OutBsel), .OutCsel(OutCsel),
    .OutDsel(OutDsel), .L_H_prime(IR_L_H_prime), .RAM_read(Ram_LOAD), .Alu_Funsel(ALU_funsel),
    .RAM_write(Ram_Write), .IR_Enable(IR_Enable), .IR_FUNSEL(IR_FUNSEL));

  // Other names for the same wires on the sheet: Z_flag = ALU_Z_C_N_O[3]

  // Notes on the sheet:
  //   OutA
  //   MuxAOut
  //   IROut (0-7)
  //   OutB
  //   Adress Reg OutD
  //   Adress Reg OutC
  //   OutALU
  //   Memory Output
endmodule
