// Logisim project arit shift right.circ as structural Verilog: 1 circuit, main circuit main
module main (
  input  [7:0] INPUT,
  output [7:0] OUTPUT
);


  assign OUTPUT = {{2{INPUT[7]}}, INPUT[6:1]};
endmodule
