// Logisim project part2b.circ as structural Verilog: 1 circuit, main circuit main
module main (
  input  Clock,
  input  [1:0] OutSelC,
  input  [7:0] _8_bit_IN,
  input  [2:0] RegSel,
  input  [1:0] FunSel,
  input  [1:0] OutSelD,
  output [7:0] OUT_C,
  output [7:0] OUT_D
);

  wire clock_1_out, or_1_out;
  wire [7:0] AR__8_bit_output, PC__8_bit_output, SP__8_bit_output;

  Hex_Digit_Display hex_digit_display_1 (.value(_8_bit_IN[3:0]));  // open: dp
  Hex_Digit_Display hex_digit_display_2 (.value(_8_bit_IN[7:4]));  // open: dp
  or or_1 (or_1_out, Clock, clock_1_out);
  Clock clock_1 (.out(clock_1_out));
  part1_8bit_main PC (
    .FunSel(FunSel), ._8_bit_Output(PC__8_bit_output), ._8_bit_Input(_8_bit_IN), .Enable(RegSel[0]),
    .CLK__do_not_use(or_1_out));  // open: out_6
  part1_8bit_main AR (
    .FunSel(FunSel), ._8_bit_Output(AR__8_bit_output), ._8_bit_Input(_8_bit_IN), .Enable(RegSel[1]),
    .CLK__do_not_use(or_1_out));  // open: out_6
  part1_8bit_main SP (
    .FunSel(FunSel), ._8_bit_Output(SP__8_bit_output), ._8_bit_Input(_8_bit_IN), .Enable(RegSel[2]),
    .CLK__do_not_use(or_1_out));  // open: out_6
  Multiplexer #(.select(2), .width(8), .enable("false")) multiplexer_1 (
    .in0(PC__8_bit_output), .in1(PC__8_bit_output), .in2(AR__8_bit_output), .in3(SP__8_bit_output),
    .out(OUT_C), .sel(OutSelC));
  Multiplexer #(.select(2), .width(8), .enable("false")) multiplexer_2 (
    .in0(PC__8_bit_output), .in1(PC__8_bit_output), .in2(AR__8_bit_output), .in3(SP__8_bit_output),
    .out(OUT_D), .sel(OutSelD));
  Hex_Digit_Display hex_digit_display_3 (.value(OUT_C[7:4]));  // open: dp
  Hex_Digit_Display hex_digit_display_4 (.value(OUT_C[3:0]));  // open: dp
  Hex_Digit_Display hex_digit_display_5 (.value(OUT_D[3:0]));  // open: dp
  Hex_Digit_Display hex_digit_display_6 (.value(OUT_D[7:4]));  // open: dp
endmodule
