// Logisim project Cunit.circ as structural Verilog: 1 circuit, main circuit main
module main (
  input  CLOCK,
  input  ZERO_FLAG_INPUT,
  input  [15:0] INSTRUCTIONS,
  output [3:0] RX_regsel,
  output [1:0] RX_funsel,
  output [1:0] OUTA,
  output [1:0] OUTB,
  output [3:0] ALU_FUN,
  output [2:0] PX_regsel,
  output [1:0] PX_funsel,
  output [1:0] OUTC,
  output [1:0] OUTD,
  output RAM_STR,
  output RAM_LD,
  output [1:0] MUXA,
  output [1:0] MUXB,
  output MUXC,
  output IR_ENABLE,
  output [1:0] IR_funsel,
  output IR_L_H_prime
);

  wire ADD_MOP, AND_MOP, CLL__CALL_MOP, clock_1_out, decoder_2_out4, decoder_4_out0, decoder_4_out15,
       decoder_5_out4, decoder_6_out4, decoder_7_out4, decoder_8_out4, decoder_9_out0, decoder_10_out4,
       DSP___DECREMENT_SP_MOP, FDW__FETCH_DOWN_MOP, FUP__FETCH_UP_MOP, IPC__INCREMENT__PC,
       ISP___INCREMENT_SP_MOP, LAR__LOAD__TO_AR_MOP, LD__LOAD__MOP, LPC__LOAD__TO_PC_MOP,
       \LSL__LOGİC_SHİFT_LEFT_MOP , \LSR__LOGİC_SHİFT_RIGHT_MOP , MOV__MOVE__MOP, multiplexer_3_out, NOT_MOP,
       or_1_out, or_2_out, or_3_out, or_4_out, or_5_out, OR_MOP, PLL__PLL_MOP, PSH___PUSH_MOP, RD__READ_MOP,
       RTR__RETURN_MOP, SDC__SELF_DECREMENT_MOP, SIN__SELF_INCREMENT_MOP, STR__STORE_MOP, SUB_MOP, undriven_4;
  wire [0:0] controlled_buffer_13_out_3, multiplexer_6_out;
  wire [1:0] adder_1_out, adder_2_out, adder_4_out, adder_5_out, controlled_buffer_1_out,
       controlled_buffer_1_out_2, controlled_buffer_1_out_5, controlled_buffer_2_out,
       controlled_buffer_2_out_3, controlled_buffer_2_out_4, controlled_buffer_3_out_2,
       controlled_buffer_3_out_3, controlled_buffer_4_out_2, controlled_buffer_8_out_2,
       controlled_buffer_8_out_3, controlled_buffer_9_out_2, controlled_buffer_9_out_3,
       controlled_buffer_10_out_2, controlled_buffer_11_out, controlled_buffer_12_out,
       controlled_buffer_12_out_3, controlled_buffer_13_out, controlled_buffer_13_out_2,
       controlled_buffer_14_out, controlled_buffer_16_out, controlled_buffer_16_out_2,
       controlled_buffer_16_out_4, controlled_buffer_16_out_6, controlled_buffer_17_out_2,
       controlled_buffer_17_out_4, controlled_buffer_18_out, controlled_buffer_18_out_2,
       controlled_buffer_19_out, rom_1_data_2;
  wire [2:0] controlled_buffer_1_out_3, controlled_buffer_4_out, controlled_buffer_7_out,
       controlled_buffer_8_out, controlled_buffer_10_out, controlled_buffer_11_out_2,
       controlled_buffer_12_out_2, controlled_buffer_13_out_4, controlled_buffer_14_out_2,
       controlled_buffer_16_out_3, controlled_buffer_17_out_3, controlled_buffer_19_out_2, decoder_2_out5,
       decoder_5_out5, decoder_6_out5, decoder_7_out5, decoder_8_out5, decoder_10_out5;
  wire [3:0] decoder_1_out0, decoder_2_out0, decoder_3_out0, decoder_5_out0, decoder_6_out0, decoder_7_out0,
       decoder_8_out0, decoder_10_out0, F1, F2, F3, multiplexer_4_out, multiplexer_5_out;
  wire [4:0] controlled_buffer_2_out_2;
  wire [5:0] controlled_buffer_5_out, controlled_buffer_18_out_3;
  wire [7:0] adder_3_out, Control_Adress_register_q, multiplexer_1_out, multiplexer_2_out, undriven_2,
       undriven_3;
  wire [7:3] controlled_buffer_7_out_2;
  wire [8:0] controlled_buffer_6_out;
  wire [9:0] controlled_buffer_3_out, controlled_buffer_9_out;
  wire [9:9] not_2_out;
  wire [11:0] rom_1_data;
  wire [16:0] controlled_buffer_1_out_4, controlled_buffer_16_out_5, controlled_buffer_17_out;
  wire [16:11] undriven, undriven_5;
  wire [16:16] not_3_out;

  buf buffer_1 (MUXC, controlled_buffer_1_out_4[16]);
  assign OUTA = controlled_buffer_1_out_5;  // Buffer buffer_2, 2 bits wide
  Adder #(.width(2)) adder_1 (.a(controlled_buffer_1_out_5), .b(2'b11), .out(adder_1_out));  // open: cin, cout
  assign OUTC = adder_1_out;  // Buffer buffer_3, 2 bits wide
  not not_1 (undriven[16], INSTRUCTIONS[7]);
  Decoder #(.select(2), .enable("false")) decoder_1 (
    .out0(decoder_1_out0[0]), .out1(decoder_1_out0[1]), .out2(decoder_1_out0[2]), .out3(decoder_1_out0[3]),
    .sel(controlled_buffer_2_out_4));
  assign RX_regsel = decoder_1_out0;  // Buffer buffer_4, 4 bits wide
  assign OUTA = controlled_buffer_3_out_3;  // Buffer buffer_5, 2 bits wide
  Adder #(.width(2)) adder_2 (.a(controlled_buffer_3_out_3), .b(2'b11), .out(adder_2_out));  // open: cin, cout
  assign OUTC = adder_2_out;  // Buffer buffer_6, 2 bits wide
  Decoder #(.select(3), .enable("false")) decoder_2 (
    .out0(decoder_2_out0[0]), .out1(decoder_2_out0[1]), .out2(decoder_2_out0[2]), .out3(decoder_2_out0[3]),
    .out4(decoder_2_out4), .out5(decoder_2_out5[0]), .out6(decoder_2_out5[1]), .out7(decoder_2_out5[2]),
    .sel(controlled_buffer_1_out_3));
  assign RX_regsel = decoder_2_out0;  // Buffer buffer_7, 4 bits wide
  buf buffer_8 (RAM_LD, controlled_buffer_2_out_2[4]);
  assign OUTD = controlled_buffer_2_out_3;  // Buffer buffer_9, 2 bits wide
  assign MUXA = controlled_buffer_2_out;  // Buffer buffer_10, 2 bits wide
  not not_2 (not_2_out[9], INSTRUCTIONS[7]);
  buf buffer_11 (MUXC, controlled_buffer_3_out[9]);
  assign OUTD = controlled_buffer_3_out_2;  // Buffer buffer_12, 2 bits wide
  Clock clock_1 (.out(clock_1_out));
  or or_1 (or_1_out, clock_1_out, CLOCK);
  assign {controlled_buffer_1_out_4[16], controlled_buffer_1_out_5, controlled_buffer_1_out_4[13:11], controlled_buffer_1_out_3, controlled_buffer_1_out_2, controlled_buffer_1_out, controlled_buffer_1_out_4[3:0]} = MOV__MOVE__MOP ? {undriven[16], INSTRUCTIONS[6:5], undriven[13:11], INSTRUCTIONS[10:8], 8'hd0} : 17'bz;  // Controlled_Buffer controlled_buffer_1
  assign MUXA = controlled_buffer_1_out_2;  // Buffer buffer_13, 2 bits wide
  assign MUXB = controlled_buffer_1_out_2;  // Buffer buffer_14, 2 bits wide
  assign PX_regsel = decoder_2_out5;  // Buffer buffer_15, 3 bits wide
  assign {controlled_buffer_2_out_4, controlled_buffer_2_out_3, controlled_buffer_2_out_2[4], controlled_buffer_2_out, controlled_buffer_2_out_2[1:0]} = RD__READ_MOP ? {INSTRUCTIONS[10:9], 7'b0110101} : 9'bz;  // Controlled_Buffer controlled_buffer_2
  assign RX_funsel = controlled_buffer_2_out_2[1:0];  // Buffer buffer_16, 2 bits wide
  assign {controlled_buffer_3_out[9], controlled_buffer_3_out_3, controlled_buffer_3_out_2, controlled_buffer_3_out[4:0]} = PSH___PUSH_MOP ? {not_2_out[9], INSTRUCTIONS[6:5], 7'b1010000} : 10'bz;  // Controlled_Buffer controlled_buffer_3
  Multiplexer #(.width(8), .enable("false")) multiplexer_1 (
    .in0(adder_3_out), .in1(multiplexer_2_out), .out(multiplexer_1_out), .sel(multiplexer_3_out));
  Multiplexer #(.select(2), .width(8), .enable("false")) multiplexer_2 (
    .in0(rom_1_data[7:0]), .in1(undriven_3), .in2(undriven_2), .in3({1'b1, INSTRUCTIONS[15:11], 2'b00}),
    .out(multiplexer_2_out), .sel(rom_1_data_2));
  assign ALU_FUN = controlled_buffer_1_out_4[3:0];  // Buffer buffer_17, 4 bits wide
  assign PX_funsel = controlled_buffer_1_out;  // Buffer buffer_18, 2 bits wide
  assign RX_funsel = controlled_buffer_1_out;  // Buffer buffer_19, 2 bits wide
  assign ALU_FUN = controlled_buffer_3_out[3:0];  // Buffer buffer_20, 4 bits wide
  buf buffer_21 (RAM_STR, controlled_buffer_3_out[4]);
  Register Control_Adress_register (
    .D(multiplexer_1_out), .Q(Control_Adress_register_q), .clk(or_1_out));  // open: en, clr
  Multiplexer #(.select(2), .enable("false")) multiplexer_3 (
    .in0(1'b1), .in1(INSTRUCTIONS[8]), .in2(undriven_4), .in3(ZERO_FLAG_INPUT), .out(multiplexer_3_out),
    .sel(rom_1_data[11:10]));
  ROM #(.dataWidth(24)) rom_1 (
    .addr(Control_Adress_register_q), .data({F1, F2, F3, rom_1_data[11:10], rom_1_data_2, rom_1_data[7:0]}),
    .sel(1'b1));
  Adder adder_3 (.a(Control_Adress_register_q), .b(8'h1), .out(adder_3_out));  // open: cin, cout
  assign PX_funsel = controlled_buffer_4_out_2;  // Buffer buffer_22, 2 bits wide
  assign PX_regsel = controlled_buffer_4_out;  // Buffer buffer_23, 3 bits wide
  assign RX_regsel = decoder_3_out0;  // Buffer buffer_24, 4 bits wide
  assign OUTB = controlled_buffer_6_out[8:7];  // Buffer buffer_25, 2 bits wide
  buf buffer_26 (RAM_LD, controlled_buffer_7_out_2[7]);
  assign OUTD = controlled_buffer_7_out_2[6:5];  // Buffer buffer_27, 2 bits wide
  assign MUXB = controlled_buffer_7_out_2[6:5];  // Buffer buffer_28, 2 bits wide
  assign MUXA = controlled_buffer_7_out_2[4:3];  // Buffer buffer_29, 2 bits wide
  assign PX_funsel = controlled_buffer_7_out_2[4:3];  // Buffer buffer_30, 2 bits wide
  assign RX_funsel = controlled_buffer_7_out_2[4:3];  // Buffer buffer_31, 2 bits wide
  assign {controlled_buffer_4_out_2, controlled_buffer_4_out} = DSP___DECREMENT_SP_MOP ? 5'b11100 : 5'bz;  // Controlled_Buffer controlled_buffer_4
  assign controlled_buffer_5_out = LD__LOAD__MOP ? {INSTRUCTIONS[10:9], 4'b0001} : 6'bz;  // Controlled_Buffer controlled_buffer_5
  Decoder #(.select(2), .enable("false")) decoder_3 (
    .out0(decoder_3_out0[0]), .out1(decoder_3_out0[1]), .out2(decoder_3_out0[2]), .out3(decoder_3_out0[3]),
    .sel(controlled_buffer_5_out[5:4]));
  assign MUXA = controlled_buffer_5_out[3:2];  // Buffer buffer_32, 2 bits wide
  assign RX_funsel = controlled_buffer_5_out[1:0];  // Buffer buffer_33, 2 bits wide
  assign OUTD = controlled_buffer_6_out[6:5];  // Buffer buffer_34, 2 bits wide
  Decoder #(.select(4), .enable("false")) decoder_4 (
    .out0(decoder_4_out0), .out1(MOV__MOVE__MOP), .out2(LD__LOAD__MOP), .out3(LPC__LOAD__TO_PC_MOP),
    .out4(LAR__LOAD__TO_AR_MOP), .out5(RD__READ_MOP), .out6(STR__STORE_MOP), .out7(CLL__CALL_MOP),
    .out8(RTR__RETURN_MOP), .out9(PSH___PUSH_MOP), .out10(PLL__PLL_MOP), .out11(SIN__SELF_INCREMENT_MOP),
    .out12(SDC__SELF_DECREMENT_MOP), .out13(DSP___DECREMENT_SP_MOP), .out14(ISP___INCREMENT_SP_MOP),
    .out15(decoder_4_out15), .sel(F1));
  assign controlled_buffer_6_out = STR__STORE_MOP ? {INSTRUCTIONS[10:9], 7'b0110001} : 9'bz;  // Controlled_Buffer controlled_buffer_6
  assign ALU_FUN = controlled_buffer_6_out[3:0];  // Buffer buffer_35, 4 bits wide
  buf buffer_36 (RAM_STR, controlled_buffer_6_out[4]);
  assign {controlled_buffer_7_out_2, controlled_buffer_7_out} = PLL__PLL_MOP ? {5'b11001, INSTRUCTIONS[10:8]} : 8'bz;  // Controlled_Buffer controlled_buffer_7
  Decoder #(.select(3), .enable("false")) decoder_5 (
    .out0(decoder_5_out0[0]), .out1(decoder_5_out0[1]), .out2(decoder_5_out0[2]), .out3(decoder_5_out0[3]),
    .out4(decoder_5_out4), .out5(decoder_5_out5[0]), .out6(decoder_5_out5[1]), .out7(decoder_5_out5[2]),
    .sel(controlled_buffer_7_out));
  assign RX_regsel = decoder_5_out0;  // Buffer buffer_37, 4 bits wide
  assign PX_regsel = decoder_5_out5;  // Buffer buffer_38, 3 bits wide
  buf buffer_39 (MUXC, controlled_buffer_9_out[9]);
  assign {controlled_buffer_8_out, controlled_buffer_8_out_2, controlled_buffer_8_out_3} = LPC__LOAD__TO_PC_MOP ? 7'b0010101 : 7'bz;  // Controlled_Buffer controlled_buffer_8
  assign PX_regsel = controlled_buffer_8_out;  // Buffer buffer_40, 3 bits wide
  assign PX_funsel = controlled_buffer_8_out_3;  // Buffer buffer_41, 2 bits wide
  assign MUXB = controlled_buffer_8_out_2;  // Buffer buffer_42, 2 bits wide
  assign PX_funsel = controlled_buffer_10_out_2;  // Buffer buffer_43, 2 bits wide
  assign RX_funsel = controlled_buffer_10_out_2;  // Buffer buffer_44, 2 bits wide
  assign {controlled_buffer_9_out[9], controlled_buffer_9_out_3, controlled_buffer_9_out_2, controlled_buffer_9_out[4:0]} = CLL__CALL_MOP ? 10'h50 : 10'bz;  // Controlled_Buffer controlled_buffer_9
  assign ALU_FUN = controlled_buffer_9_out[3:0];  // Buffer buffer_45, 4 bits wide
  buf buffer_46 (RAM_STR, controlled_buffer_9_out[4]);
  assign OUTD = controlled_buffer_9_out_2;  // Buffer buffer_47, 2 bits wide
  assign OUTC = controlled_buffer_9_out_3;  // Buffer buffer_48, 2 bits wide
  assign {controlled_buffer_10_out_2, controlled_buffer_10_out} = SIN__SELF_INCREMENT_MOP ? {2'b10, INSTRUCTIONS[10:8]} : 5'bz;  // Controlled_Buffer controlled_buffer_10
  Decoder #(.select(3), .enable("false")) decoder_6 (
    .out0(decoder_6_out0[0]), .out1(decoder_6_out0[1]), .out2(decoder_6_out0[2]), .out3(decoder_6_out0[3]),
    .out4(decoder_6_out4), .out5(decoder_6_out5[0]), .out6(decoder_6_out5[1]), .out7(decoder_6_out5[2]),
    .sel(controlled_buffer_10_out));
  assign RX_regsel = decoder_6_out0;  // Buffer buffer_49, 4 bits wide
  assign PX_regsel = decoder_6_out5;  // Buffer buffer_50, 3 bits wide
  assign PX_funsel = controlled_buffer_11_out;  // Buffer buffer_51, 2 bits wide
  assign {controlled_buffer_11_out, controlled_buffer_11_out_2} = ISP___INCREMENT_SP_MOP ? 5'b10100 : 5'bz;  // Controlled_Buffer controlled_buffer_11
  assign PX_regsel = controlled_buffer_11_out_2;  // Buffer buffer_52, 3 bits wide
  assign MUXB = controlled_buffer_12_out;  // Buffer buffer_53, 2 bits wide
  assign PX_regsel = controlled_buffer_12_out_2;  // Buffer buffer_54, 3 bits wide
  assign PX_regsel = controlled_buffer_13_out_4;  // Buffer buffer_55, 3 bits wide
  assign PX_funsel = controlled_buffer_14_out;  // Buffer buffer_56, 2 bits wide
  assign RX_funsel = controlled_buffer_14_out;  // Buffer buffer_57, 2 bits wide
  assign {controlled_buffer_12_out_2, controlled_buffer_12_out, controlled_buffer_12_out_3} = LAR__LOAD__TO_AR_MOP ? 7'b0100101 : 7'bz;  // Controlled_Buffer controlled_buffer_12
  assign PX_funsel = controlled_buffer_12_out_3;  // Buffer buffer_58, 2 bits wide
  assign {controlled_buffer_13_out_4, controlled_buffer_13_out, controlled_buffer_13_out_2, controlled_buffer_13_out_3[0]} = RTR__RETURN_MOP ? 8'h2d : 8'bz;  // Controlled_Buffer controlled_buffer_13
  assign PX_funsel = controlled_buffer_13_out;  // Buffer buffer_59, 2 bits wide
  assign {controlled_buffer_14_out, controlled_buffer_14_out_2} = SDC__SELF_DECREMENT_MOP ? {2'b11, INSTRUCTIONS[10:8]} : 5'bz;  // Controlled_Buffer controlled_buffer_14
  Decoder #(.select(3), .enable("false")) decoder_7 (
    .out0(decoder_7_out0[0]), .out1(decoder_7_out0[1]), .out2(decoder_7_out0[2]), .out3(decoder_7_out0[3]),
    .out4(decoder_7_out4), .out5(decoder_7_out5[0]), .out6(decoder_7_out5[1]), .out7(decoder_7_out5[2]),
    .sel(controlled_buffer_14_out_2));
  assign RX_regsel = decoder_7_out0;  // Buffer buffer_60, 4 bits wide
  buf buffer_61 (RAM_LD, controlled_buffer_13_out_3[0]);
  assign MUXB = controlled_buffer_13_out_2;  // Buffer buffer_62, 2 bits wide
  assign PX_regsel = decoder_7_out5;  // Buffer buffer_63, 3 bits wide
  or or_2 (or_2_out, MOV__MOVE__MOP, LD__LOAD__MOP, LPC__LOAD__TO_PC_MOP, LAR__LOAD__TO_AR_MOP, RD__READ_MOP, ISP___INCREMENT_SP_MOP, DSP___DECREMENT_SP_MOP, SDC__SELF_DECREMENT_MOP, SIN__SELF_INCREMENT_MOP, PLL__PLL_MOP, RTR__RETURN_MOP, ADD_MOP, SUB_MOP, AND_MOP, OR_MOP, NOT_MOP, IPC__INCREMENT__PC, FDW__FETCH_DOWN_MOP, FUP__FETCH_UP_MOP, \LSR__LOGİC_SHİFT_RIGHT_MOP , \LSL__LOGİC_SHİFT_LEFT_MOP );
  assign RAM_STR = or_2_out ? 1'b0 : 1'bz;  // Controlled_Buffer controlled_buffer_15
  buf buffer_64 (MUXC, controlled_buffer_16_out_5[16]);
  assign OUTA = controlled_buffer_16_out_6;  // Buffer buffer_65, 2 bits wide
  Adder #(.width(2)) adder_4 (.a(controlled_buffer_16_out_6), .b(2'b11), .out(adder_4_out));  // open: cin, cout
  assign OUTC = adder_4_out;  // Buffer buffer_66, 2 bits wide
  not not_3 (not_3_out[16], INSTRUCTIONS[7]);
  assign OUTB = controlled_buffer_16_out_4;  // Buffer buffer_67, 2 bits wide
  Decoder #(.select(3), .enable("false")) decoder_8 (
    .out0(decoder_8_out0[0]), .out1(decoder_8_out0[1]), .out2(decoder_8_out0[2]), .out3(decoder_8_out0[3]),
    .out4(decoder_8_out4), .out5(decoder_8_out5[0]), .out6(decoder_8_out5[1]), .out7(decoder_8_out5[2]),
    .sel(controlled_buffer_16_out_3));
  assign RX_regsel = decoder_8_out0;  // Buffer buffer_68, 4 bits wide
  Multiplexer #(.select(4), .width(4), .enable("false")) multiplexer_4 (
    .in1(4'b0100), .in2(4'b0110), .in4(4'b0111), .in8(4'b1000), .out(multiplexer_4_out),
    .sel({OR_MOP, AND_MOP, SUB_MOP, ADD_MOP}));  // open: in0, in3, in5, in6, in7, in9, in10, in11, in12, in13, in14, in15
  or or_3 (or_3_out, ADD_MOP, SUB_MOP, AND_MOP, OR_MOP);
  assign {controlled_buffer_16_out_5[16], controlled_buffer_16_out_6, controlled_buffer_16_out_5[13], controlled_buffer_16_out_4, controlled_buffer_16_out_3, controlled_buffer_16_out_2, controlled_buffer_16_out, controlled_buffer_16_out_5[3:0]} = or_3_out ? {not_3_out[16], INSTRUCTIONS[6:2], INSTRUCTIONS[10:8], 4'b1101, multiplexer_4_out} : 17'bz;  // Controlled_Buffer controlled_buffer_16
  assign MUXA = controlled_buffer_16_out_2;  // Buffer buffer_69, 2 bits wide
  assign MUXB = controlled_buffer_16_out_2;  // Buffer buffer_70, 2 bits wide
  assign PX_regsel = decoder_8_out5;  // Buffer buffer_71, 3 bits wide
  assign ALU_FUN = controlled_buffer_16_out_5[3:0];  // Buffer buffer_72, 4 bits wide
  assign PX_funsel = controlled_buffer_16_out;  // Buffer buffer_73, 2 bits wide
  assign RX_funsel = controlled_buffer_16_out;  // Buffer buffer_74, 2 bits wide
  buf buffer_75 (MUXC, controlled_buffer_17_out[16]);
  assign OUTA = controlled_buffer_17_out_4;  // Buffer buffer_76, 2 bits wide
  Adder #(.width(2)) adder_5 (.a(controlled_buffer_17_out_4), .b(2'b11), .out(adder_5_out));  // open: cin, cout
  assign OUTC = adder_5_out;  // Buffer buffer_77, 2 bits wide
  Decoder #(.select(4), .enable("false")) decoder_9 (
    .out0(decoder_9_out0), .out1(ADD_MOP), .out2(SUB_MOP), .out3(AND_MOP), .out4(OR_MOP), .out5(NOT_MOP),
    .out6(\LSL__LOGİC_SHİFT_LEFT_MOP ), .out7(\LSR__LOGİC_SHİFT_RIGHT_MOP ), .out8(FUP__FETCH_UP_MOP),
    .out9(FDW__FETCH_DOWN_MOP), .out10(IPC__INCREMENT__PC), .sel(F2));  // open: out11, out12, out13, out14, out15
  not not_4 (undriven_5[16], INSTRUCTIONS[7]);
  Decoder #(.select(3), .enable("false")) decoder_10 (
    .out0(decoder_10_out0[0]), .out1(decoder_10_out0[1]), .out2(decoder_10_out0[2]),
    .out3(decoder_10_out0[3]), .out4(decoder_10_out4), .out5(decoder_10_out5[0]), .out6(decoder_10_out5[1]),
    .out7(decoder_10_out5[2]), .sel(controlled_buffer_17_out_3));
  assign RX_regsel = decoder_10_out0;  // Buffer buffer_78, 4 bits wide
  Multiplexer #(.select(3), .width(4), .enable("false")) multiplexer_5 (
    .in1(4'b0010), .in2(4'b1010), .in4(4'b1011), .out(multiplexer_5_out),
    .sel({\LSR__LOGİC_SHİFT_RIGHT_MOP , \LSL__LOGİC_SHİFT_LEFT_MOP , NOT_MOP}));  // open: in0, in3, in5, in6, in7
  or or_4 (or_4_out, NOT_MOP, \LSL__LOGİC_SHİFT_LEFT_MOP , \LSR__LOGİC_SHİFT_RIGHT_MOP );
  assign {controlled_buffer_17_out[16], controlled_buffer_17_out_4, controlled_buffer_17_out[13:11], controlled_buffer_17_out_3, controlled_buffer_17_out_2, controlled_buffer_17_out[5:0]} = or_4_out ? {undriven_5[16], INSTRUCTIONS[6:5], undriven_5[13:11], INSTRUCTIONS[10:8], 4'b1101, multiplexer_5_out} : 17'bz;  // Controlled_Buffer controlled_buffer_17
  assign MUXA = controlled_buffer_17_out_2;  // Buffer buffer_79, 2 bits wide
  assign MUXB = controlled_buffer_17_out_2;  // Buffer buffer_80, 2 bits wide
  assign PX_regsel = decoder_10_out5;  // Buffer buffer_81, 3 bits wide
  assign ALU_FUN = controlled_buffer_17_out[3:0];  // Buffer buffer_82, 4 bits wide
  assign PX_funsel = controlled_buffer_17_out[5:4];  // Buffer buffer_83, 2 bits wide
  assign RX_funsel = controlled_buffer_17_out[5:4];  // Buffer buffer_84, 2 bits wide
  buf buffer_85 (RAM_LD, controlled_buffer_18_out_3[5]);
  buf buffer_86 (IR_ENABLE, controlled_buffer_18_out_3[5]);
  assign IR_funsel = controlled_buffer_18_out;  // Buffer buffer_87, 2 bits wide
  or or_5 (or_5_out, FDW__FETCH_DOWN_MOP, FUP__FETCH_UP_MOP);
  assign {controlled_buffer_18_out_3[5], controlled_buffer_18_out, controlled_buffer_18_out_2, controlled_buffer_18_out_3[0]} = or_5_out ? {5'b11100, multiplexer_6_out[0]} : 6'bz;  // Controlled_Buffer controlled_buffer_18
  buf buffer_88 (IR_L_H_prime, controlled_buffer_18_out_3[0]);
  assign OUTD = controlled_buffer_18_out_2;  // Buffer buffer_89, 2 bits wide
  Multiplexer #(.enable("false")) multiplexer_6 (
    .in0(1'b0), .in1(1'b1), .out(multiplexer_6_out[0]), .sel(FDW__FETCH_DOWN_MOP));
  assign PX_funsel = controlled_buffer_19_out;  // Buffer buffer_90, 2 bits wide
  assign {controlled_buffer_19_out, controlled_buffer_19_out_2} = IPC__INCREMENT__PC ? 5'b10001 : 5'bz;  // Controlled_Buffer controlled_buffer_19
  assign PX_regsel = controlled_buffer_19_out_2;  // Buffer buffer_91, 3 bits wide

  // Other names for the same wires on the sheet: IR_11 = INSTRUCTIONS[11]; OPCODE[4:0] = INSTRUCTIONS[15:11];
  //   IR_12 = INSTRUCTIONS[12]; IR_13 = INSTRUCTIONS[13]; IR_14 = INSTRUCTIONS[14]; IR_15 = INSTRUCTIONS[15];
  //   ADDRESS[7:0] = INSTRUCTIONS[7:0]; IR_2 = INSTRUCTIONS[2]; SRCREG2[2:0] = INSTRUCTIONS[4:2];
  //   IR_3 = INSTRUCTIONS[3]; IR_4 = INSTRUCTIONS[4]; ADRESSING_MODE = INSTRUCTIONS[8];
  //   DESTREG[2:0] = INSTRUCTIONS[10:8]; IR_8 = INSTRUCTIONS[8]; IR_9 = INSTRUCTIONS[9];
  //   IR_9_10[1:0] = INSTRUCTIONS[10:9]; IR_10 = INSTRUCTIONS[10]; IR_5 = INSTRUCTIONS[5];
  //   SRCREG1[2:0] = INSTRUCTIONS[7:5]; IR_6 = INSTRUCTIONS[6]; IR_0 = INSTRUCTIONS[0]; IR_1 = INSTRUCTIONS[1];
  //   IR_7 = INSTRUCTIONS[7]; ZERO_FLAG = ZERO_FLAG_INPUT

  // Notes on the sheet:
  //   Subroutine CALL AND RETURN we didnot use this
  //   MOVE MOP
  //   Mapping
  //   READ MOP
  //   PUSH MOP
  //   Assume 100 for destreg will not be  given only 101  for  pc
  //   contents of rom_1 (hex, n*v repeats v):
  //   80001 a0002 90003 a0300 124*0 482 200000 500000 0 486 0 600000 0 100000 0 0 0 d0008d 900000 0 0
  //   a00091 e00000 0 0 10000 0 0 0 20000 0 0 0 10009d c00000 0 0 1000a1 b00000 0 0 30000 0 0 0 40000 0 0
  //   0 50000 0 0 0 60000 0 0 0 70000 0 0 0 400 300000 0 0 400 cbf 0 300000 400 c00 300000 0 400 d000c6
  //   7000c7 300000 8000c9 e00000
  //   İncrementer
  //   Condition for branching and  branching field 2+2 4 bits
  //   DECREMENT SP MOP
  //   4 bit each can be changed
  //   LOAD MOP
  //   STORE MOP
  //   PULL MOP
  //   Next  address  part  in the  instruction 8 bit cuz rom address
  //   Rest of  the instruction F1/F2/F3/branch / condition etc 16 bit
  //   LOAD TO PC MOP
  //   CALL MOP
  //   SELF INCREMENT MOP
  //   INCREMENT SP MOP
  //   LOAD TO AR MOP
  //   RETURN MOP
  //   SELF DECREMENT MOP
  //   ADD/SUB/AND/OR MOP
  //   Assume 100 for destreg will not be  given only 101  for  pc
  //   NOT/LSL/LSR MOP
  //   FETCH UP/DOWN MOP
  //   INCREMENT PC MOP
endmodule
