// Logisim project circ shift left.circ as structural Verilog: 1 circuit, main circuit main
module main (
  input  [7:0] INPUT,
  output [7:0] OUTPUT,
  output CARRY,
  output OVERFLOW
);

  xor xor_1 (OVERFLOW, INPUT[6], INPUT[7]);

  assign CARRY = INPUT[7];
  assign OUTPUT = {INPUT[6:0], INPUT[7]};
endmodule
