// Logisim project part2a.circ as structural Verilog: 1 circuit, main circuit main
module main (
  input  Clock,
  input  [7:0] _8_bit_IN,
  input  [1:0] OutSelA,
  input  [3:0] RegSel,
  input  [1:0] OutSelB,
  input  [1:0] FunSel,
  output [7:0] OutA,
  output [7:0] OutB
);

  wire clock_1_out, or_1_out;
  wire [7:0] R0__8_bit_output, R1__8_bit_output, R2__8_bit_output, R3__8_bit_output;

  Hex_Digit_Display hex_digit_display_1 (.value(_8_bit_IN[7:4]));  // open: dp
  Hex_Digit_Display hex_digit_display_2 (.value(_8_bit_IN[3:0]));  // open: dp
  Clock clock_1 (.out(clock_1_out));
  or or_1 (or_1_out, Clock, clock_1_out);
  part1_8bit_main R0 (
    .FunSel(FunSel), ._8_bit_Output(R0__8_bit_output), ._8_bit_Input(_8_bit_IN), .Enable(RegSel[0]),
    .CLK__do_not_use(or_1_out));  // open: out_6
  part1_8bit_main R1 (
    .FunSel(FunSel), ._8_bit_Output(R1__8_bit_output), ._8_bit_Input(_8_bit_IN), .Enable(RegSel[1]),
    .CLK__do_not_use(or_1_out));  // open: out_6
  part1_8bit_main R2 (
    .FunSel(FunSel), ._8_bit_Output(R2__8_bit_output), ._8_bit_Input(_8_bit_IN), .Enable(RegSel[2]),
    .CLK__do_not_use(or_1_out));  // open: out_6
  part1_8bit_main R3 (
    .FunSel(FunSel), ._8_bit_Output(R3__8_bit_output), ._8_bit_Input(_8_bit_IN), .Enable(RegSel[3]),
    .CLK__do_not_use(or_1_out));  // open: out_6
  Multiplexer #(.select(2), .width(8), .enable("false")) multiplexer_1 (
    .in0(R0__8_bit_output), .in1(R1__8_bit_output), .in2(R2__8_bit_output), .in3(R3__8_bit_output),
    .out(OutA), .sel(OutSelA));
  Multiplexer #(.select(2), .width(8), .enable("false")) multiplexer_2 (
    .in0(R0__8_bit_output), .in1(R1__8_bit_output), .in2(R2__8_bit_output), .in3(R3__8_bit_output),
    .out(OutB), .sel(OutSelB));
  Hex_Digit_Display hex_digit_display_3 (.value(OutA[7:4]));  // open: dp
  Hex_Digit_Display hex_digit_display_4 (.value(OutB[7:4]));  // open: dp
  Hex_Digit_Display hex_digit_display_5 (.value(OutA[3:0]));  // open: dp
  Hex_Digit_Display hex_digit_display_6 (.value(OutB[3:0]));  // open: dp
endmodule
